# Fritzing sketch 1.LED闪烁实验 (saved by Fritzing 0.8.3b)
breadboards: 1

parts:
  R1 = Resistor [tolerance=±5% resistance=1k package=THT]
  LED1 = LED - 5mm [color="Red (633nm)" package="5 mm [THT]"]
  元件1 = Arduino Uno (Rev3)
  LED2 = LED - 5mm [color="Red (633nm)" package="5 mm [THT]"]
  R2 = Resistor [tolerance=±5% resistance=1k package=THT]

nets:
  N1: R1.Pin_0, 元件1.D2
  N2: R1.Pin_1, LED1.cathode
  N3: LED1.anode, 元件1.5V
  N4: 元件1.GND, R2.Pin_0
  N5: 元件1.D3_PWM, LED2.anode
  N6: LED2.cathode, R2.Pin_1

notes:
  LED长正短负
  正
