# Fritzing sketch 10.四位共阴数码管实验 (saved by Fritzing 0.8.3b)

parts:
  元件1 = Arduino Uno (Rev3)
  R1 = Resistor [tolerance=±5% resistance=220 package=THT]
  R2 = Resistor [tolerance=±5% resistance=220 package=THT]
  R3 = Resistor [tolerance=±5% resistance=220 package=THT]
  R4 = Resistor [tolerance=±5% resistance=220 package=THT]
  DI1 = 4位共阴数码管 [package=THT]

nets:
  N1: 元件1.ICSP_SCK, 元件1.D13/SCK, R3.Pin_1
  N2: 元件1.D8, DI1.cathodeG
  N3: 元件1.D9_PWM, DI1.cathodeDP
  N4: 元件1.D10_PWM/SS, R4.Pin_0
  N5: 元件1.D11_PWM/MOSI, R1.Pin_0
  N6: 元件1.D12/MISO, R2.Pin_0
  N7: 元件1.D2, DI1.cathodeA
  N8: 元件1.D3_PWM, DI1.cathodeB
  N9: 元件1.D4, DI1.cathodeC
  N10: 元件1.D5_PWM, DI1.cathodeD
  N11: 元件1.D6_PWM, DI1.cathodeE
  N12: 元件1.D7, DI1.cathodeF
  N13: R1.Pin_1, DI1.com2
  N14: R2.Pin_1, DI1.com3
  N15: R3.Pin_0, DI1.com4
  N16: R4.Pin_1, DI1.com1
