# Fritzing sketch 13.温度传感器LM35实验 (saved by Fritzing 0.8.3b)
breadboards: 1

parts:
  元件1 = Arduino Uno (Rev3)
  T1 = LM35 Temperature Sensor [package="TO92 [THT]"]

nets:
  N1: 元件1.A0, T1.Vout
  GND: 元件1.GND, T1.GND
  N2: 元件1.5V, T1.+Vs
