# Fritzing sketch 14.液晶LCD1602实验 (saved by Fritzing 0.8.3b)
breadboards: 1

parts:
  元件1 = Arduino Uno (Rev3)
  LCD1 = LCD screen
  R1 = Resistor [tolerance=±5% resistance=4.7k package=THT]
  T1 = LM35 Temperature Sensor [package="TO92 [THT]"]

nets:
  N1: 元件1.A0, T1.Vout
  GND: 元件1.GND, LCD1.VSS, LCD1.R/W, LCD1.LED-, R1.Pin_0, T1.GND
  N2: 元件1.D11_PWM/MOSI, LCD1.E
  N3: 元件1.D12/MISO, LCD1.RS
  N4: 元件1.D2, LCD1.DB7
  N5: 元件1.D3_PWM, LCD1.DB6
  N6: 元件1.D4, LCD1.DB5
  N7: 元件1.D5_PWM, LCD1.DB4
  5V: 元件1.5V, LCD1.VDD, LCD1.LED+, T1.+Vs
  N8: LCD1.V0, R1.Pin_1
