# Fritzing sketch 15.滚珠开关实验 (saved by Fritzing 0.8.3b)
breadboards: 1

parts:
  元件1 = Arduino Uno (Rev3)
  S1 = Tilt Switch [package=THT]
  J1 = Piezo Speaker

nets:
  N1: 元件1.GND, S1.Pin_1, J1.pin1
  N2: 元件1.D2, S1.Pin_2
  N3: 元件1.D3_PWM, J1.pin2

notes:
  滚珠开关
  有源蜂鸣器
