# Fritzing sketch 16.火焰传感器实验 (saved by Fritzing 0.8.3b)
breadboards: 1

parts:
  元件1 = Arduino Uno (Rev3)
  LED1 = LED - 5mm [color="Red (633nm)" package="5 mm [THT]"]
  R1 = Resistor [tolerance=±5% resistance=10k package=THT]
  J1 = Piezo Speaker

nets:
  N1: 元件1.A0, LED1.cathode, R1.Pin_1
  N2: 元件1.GND, R1.Pin_0, J1.pin1
  N3: 元件1.D2, J1.pin2
  N4: 元件1.5V, LED1.anode

notes:
  火焰传感器
  有源蜂鸣器
