# Fritzing sketch 18.按键切换LED颜色实验 (saved by Fritzing 0.8.3b)
breadboards: 1

parts:
  元件1 = Arduino Uno (Rev3)
  LED1 = RGB LED (com. anode, rbg) [package="5 mm [THT]"]
  R1 = Resistor [tolerance=±5% resistance=1k package=THT]
  R2 = Resistor [tolerance=±5% resistance=1k package=THT]
  R3 = Resistor [tolerance=±5% resistance=1k package=THT]
  S1 = Pushbutton [package="[THT]"]

nets:
  N1: 元件1.GND, S1.Pin_3, S1.Pin_4
  N2: 元件1.D2, R1.Pin_0
  N3: 元件1.D3_PWM, R3.Pin_0
  N4: 元件1.D4, R2.Pin_0
  N5: 元件1.D5_PWM, S1.Pin_1, S1.Pin_2
  N6: 元件1.5V, LED1.common_anode
  N7: LED1.red_cathode, R1.Pin_1
  N8: LED1.blue_cathode, R3.Pin_1
  N9: LED1.green_cathode, R2.Pin_1
