# Fritzing sketch 20.74HC595实验 (saved by Fritzing 0.8.3b)
breadboards: 1

parts:
  元件1 = Arduino Uno (Rev3)
  U1 = 74HC595 [package="DIP16 [THT]"]
  LED1 = LED - 5mm [color="Red (633nm)" package="5 mm [THT]"]
  LED2 = LED - 5mm [color="Red (633nm)" package="5 mm [THT]"]
  LED3 = LED - 5mm [color="Red (633nm)" package="5 mm [THT]"]
  LED4 = LED - 5mm [color="Red (633nm)" package="5 mm [THT]"]
  LED5 = LED - 5mm [color="Red (633nm)" package="5 mm [THT]"]
  LED6 = LED - 5mm [color="Red (633nm)" package="5 mm [THT]"]
  LED7 = LED - 5mm [color="Red (633nm)" package="5 mm [THT]"]
  LED8 = LED - 5mm [color="Red (633nm)" package="5 mm [THT]"]
  R1 = Resistor [tolerance=±5% resistance=220 package=THT]
  R2 = Resistor [tolerance=±5% resistance=220 package=THT]
  R3 = Resistor [tolerance=±5% resistance=220 package=THT]
  R4 = Resistor [tolerance=±5% resistance=220 package=THT]
  R5 = Resistor [tolerance=±5% resistance=220 package=THT]
  R6 = Resistor [tolerance=±5% resistance=220 package=THT]
  R7 = Resistor [tolerance=±5% resistance=220 package=THT]
  R8 = Resistor [tolerance=±5% resistance=220 package=THT]

nets:
  GND: 元件1.GND, U1.GND, U1.OE, R1.Pin_0, R2.Pin_0, R3.Pin_0, R4.Pin_0, R5.Pin_0, R6.Pin_0, R7.Pin_0, R8.Pin_0
  N1: 元件1.D8, U1.ST_CP
  N2: 元件1.D11_PWM/MOSI, U1.DS
  N3: 元件1.D12/MISO, U1.SH_CP
  5V: 元件1.5V, U1.MR, U1.VCC
  N4: U1.Q1, LED2.anode
  N5: U1.Q2, LED3.anode
  N6: U1.Q3, LED4.anode
  N7: U1.Q4, LED5.anode
  N8: U1.Q5, LED6.anode
  N9: U1.Q6, LED7.anode
  N10: U1.Q7, LED8.anode
  N11: U1.Q0, LED1.anode
  N12: LED1.cathode, R6.Pin_1
  N13: LED2.cathode, R7.Pin_1
  N14: LED3.cathode, R8.Pin_1
  N15: LED4.cathode, R1.Pin_1
  N16: LED5.cathode, R2.Pin_1
  N17: LED6.cathode, R3.Pin_1
  N18: LED7.cathode, R4.Pin_1
  N19: LED8.cathode, R5.Pin_1
