# Fritzing sketch 21.8_8点阵实验 (saved by Fritzing 0.8.3b)
breadboards: 2

parts:
  元件1 = Arduino Uno (Rev3)
  U1 = 8*8点阵模块

nets:
  N1: 元件1.A2, U1.H8
  N2: 元件1.A3, U1.L5
  N3: 元件1.A4/SDA, U1.H6
  N4: 元件1.A5/SCL, U1.H3
  N5: 元件1.ICSP_MISO, 元件1.D12/MISO, U1.H7
  N6: 元件1.ICSP_SCK, 元件1.D13/SCK, U1.H5
  N7: 元件1.ICSP_MOSI, 元件1.D11_PWM/MOSI, U1.L2
  N8: 元件1.D8, U1.L7
  N9: 元件1.D9_PWM, U1.L8
  N10: 元件1.D10_PWM/SS, U1.L3
  N11: 元件1.D2, U1.H1
  N12: 元件1.D3_PWM, U1.L4
  N13: 元件1.D4, U1.L6
  N14: 元件1.D5_PWM, U1.H4
  N15: 元件1.D6_PWM, U1.L1
  N16: 元件1.D7, U1.H2

notes:
  1.面包板是可以自己组合的，
  2.套件内配备两块一样的面包板
  3.因受本实验中点阵宽度限制，必须使用两块面包板搭配使用
  4.两块面包板按照如图方式级联：
  将其中一块面包板的电源/地的那行，折弯90度
  将两块面包板级联成如图所示的外观，即可做本实验
