# Fritzing sketch 22.9克舵机实验 (saved by Fritzing 0.8.3b)
breadboards: 1

parts:
  元件1 = Arduino Uno (Rev3)
  J1 = Basic Servo
  R3 = Trimmer Potentiometer [maximum_resistance=10kΩ package=THT]

nets:
  N1: 元件1.A5/SCL, R3.wiper
  GND: 元件1.GND, J1.gnd, R3.leg2
  N2: 元件1.D9_PWM, J1.pulse
  5V: 元件1.5V, J1.vcc, R3.leg1
