# Fritzing sketch 25.虚拟鼠标实验 (saved by Fritzing 0.8.3b)
breadboards: 1

parts:
  元件1 = Arduino Leonardo (Rev3b)
  S1 = Pushbutton [package="[THT]"]
  S2 = Pushbutton [package="[THT]"]
  S3 = Pushbutton [package="[THT]"]

nets:
  N1: 元件1.D2/SDA, S2.Pin_3, S2.Pin_4
  N2: 元件1.D3_PWM/SCL, S1.Pin_3, S1.Pin_4
  N3: 元件1.D4/A6, S3.Pin_3, S3.Pin_4
  N4: 元件1.GND, S1.Pin_1, S1.Pin_2, S2.Pin_1, S2.Pin_2, S3.Pin_1, S3.Pin_2
