# Fritzing sketch 26.直流电机驱动实验 (saved by Fritzing 0.8.3b)

parts:
  元件1 = Arduino Uno (Rev3)
  U1 = L9110电机驱动

nets:
  GND: 元件1.GND, U1.GND
  N1: 元件1.D5_PWM, U1.IB
  N2: 元件1.D6_PWM, U1.IA
  5V: 元件1.5V, U1.VCC
