# Fritzing sketch 27.风扇转速调节实验 (saved by Fritzing 0.8.3b)

parts:
  元件1 = Arduino Uno (Rev3)
  U1 = L9110电机驱动
  R1 = Trimmer Potentiometer [maximum_resistance=10kΩ package=THT]

nets:
  N1: 元件1.A0, R1.wiper
  GND: 元件1.GND, U1.GND, R1.leg2
  N2: 元件1.D5_PWM, U1.IB
  N3: 元件1.D6_PWM, U1.IA
  N4: 元件1.ioref, R1.leg1
  5V: 元件1.5V, U1.VCC
