# Fritzing sketch 3.按键控制LED实验 (saved by Fritzing 0.8.3b)
breadboards: 1

parts:
  元件1 = Arduino Uno (Rev3)
  S1 = Pushbutton [package="[THT]"]

nets:
  N1: 元件1.GND, S1.Pin_3, S1.Pin_4
  N2: 元件1.D2, S1.Pin_1, S1.Pin_2
