# Fritzing sketch 30.手机和蓝牙模块通讯实验 (saved by Fritzing 0.8.3b)
breadboards: 1

parts:
  元件1 = Arduino Uno (Rev3)
  U2 = HX711

nets:
  GND: 元件1.GND, U2.GND
  N1: 元件1.D0/RX, U2.TXD
  N2: 元件1.D1/TX, U2.RXD
  5V: 元件1.5V, U2.VCC
