# Fritzing sketch 31.手机蓝牙控制继电器实验 (saved by Fritzing 0.8.3b)
breadboards: 1

parts:
  元件1 = Arduino Uno (Rev3)
  U2 = HX711
  U3 = 蜂鸣器模块

nets:
  GND: 元件1.GND, U2.GND
  N1: 元件1.D0/RX, U2.TXD
  N2: 元件1.D1/TX, U2.RXD
  N3: 元件1.D2, U3.IO
  5V: 元件1.5V, U2.VCC, U3.VCC
