# Fritzing sketch 34.实时时钟DS1302实验 (saved by Fritzing 0.8.3b)
breadboards: 1

parts:
  元件1 = Arduino Uno (Rev3)
  U1 = 实时时钟模块DS1302
  S1 = Pushbutton [package="[THT]"]
  S2 = Pushbutton [package="[THT]"]
  S3 = Pushbutton [package="[THT]"]
  S4 = Pushbutton [package="[THT]"]

nets:
  GND: 元件1.GND, U1.GND, S1.Pin_1, S1.Pin_2, S2.Pin_1, S2.Pin_2, S3.Pin_1, S3.Pin_2, S4.Pin_3, S4.Pin_4
  N1: 元件1.D8, S4.Pin_1, S4.Pin_2
  N2: 元件1.D2, U1.RST
  N3: 元件1.D3_PWM, U1.DAT
  N4: 元件1.D4, U1.CLK
  N5: 元件1.D5_PWM, S1.Pin_3, S1.Pin_4
  N6: 元件1.D6_PWM, S2.Pin_3, S2.Pin_4
  N7: 元件1.D7, S3.Pin_3, S3.Pin_4
  5V: 元件1.5V, U1.VCC
