# Fritzing sketch 35.烟雾传感器MQ-2实验 (saved by Fritzing 0.8.3b)

parts:
  元件1 = Arduino Uno (Rev3)
  U1 = MQ系列传感器

nets:
  N1: 元件1.A5/SCL, U1.AO
  GND: 元件1.GND, U1.GND
  N2: 元件1.D2, U1.DO
  5V: 元件1.5V, U1.VCC
