# Fritzing sketch 36.超声波模块实验 (saved by Fritzing 0.8.3b)

parts:
  元件1 = Arduino Uno (Rev3)
  元件2 = HC-SR04

nets:
  GND: 元件1.GND, 元件2.GND
  N1: 元件1.D2, 元件2.Trig
  N2: 元件1.D3_PWM, 元件2.Echo
  5V: 元件1.5V, 元件2.VCC
