# Fritzing sketch 37.电子秤制作实验 (saved by Fritzing 0.8.3b)

parts:
  元件1 = Arduino Uno (Rev3)
  U1 = HX711
  U2 = HX711

nets:
  GND: 元件1.GND, U1.GND
  N1: 元件1.D2, U1.SCK
  N2: 元件1.D3_PWM, U1.DT
  5V: 元件1.5V, U1.VCC
  N3: U1.E+, U2.PIN1
  N4: U1.E-, U2.PIN2
  N5: U1.A-, U2.PIN3
  N6: U1.A+, U2.PIN4
