# Fritzing sketch 38.RFID实验 (saved by Fritzing 0.8.3b)

parts:
  U4 = RC522
  U5 = 继电器模块
  元件2 = Arduino Uno (Rev3)

nets:
  N1: U4.SDA, 元件2.D10_PWM/SS
  N2: U4.SCK, 元件2.ICSP_SCK, 元件2.D13/SCK
  N3: U4.MOSI, 元件2.ICSP_MOSI, 元件2.D11_PWM/MOSI
  N4: U4.MISO, 元件2.ICSP_MISO, 元件2.D12/MISO
  GND: U4.GND, U5.GND, 元件2.GND
  N5: U4.RST, 元件2.D9_PWM
  3.3V: U4.3.3V, 元件2.3V3
  N6: U5.IO, 元件2.D2
  VCC: U5.VCC, 元件2.5V

custom parts:
  继电器模块: 蜂鸣器模块
