# Fritzing sketch 39.GSM模块拨打电话实验 (saved by Fritzing 0.8.3b)
breadboards: 1

parts:
  元件1 = Arduino Uno (Rev3)
  U1 = SIM900A
  S1 = Pushbutton [package="[THT]"]
  S2 = Pushbutton [package="[THT]"]

nets:
  GND: 元件1.GND, U1.GND, S1.Pin_1, S1.Pin_2, S2.Pin_1, S2.Pin_2
  N1: 元件1.D0/RX, U1.TXD
  N2: 元件1.D1/TX, U1.RXD
  N3: 元件1.D2, S1.Pin_3, S1.Pin_4
  N4: 元件1.D3_PWM, S2.Pin_3, S2.Pin_4
  5V: 元件1.5V
