# Fritzing sketch 4.有源蜂鸣器实验 (saved by Fritzing 0.8.3b)
breadboards: 1

parts:
  元件1 = Arduino Uno (Rev3)
  S1 = Pushbutton [package="[THT]"]
  J1 = Piezo Speaker

nets:
  N1: 元件1.GND, S1.Pin_3, S1.Pin_4, J1.pin1
  N2: 元件1.D2, S1.Pin_1, S1.Pin_2
  N3: 元件1.D3_PWM, J1.pin2

notes:
  有源蜂鸣器
