# Fritzing sketch 6.PWM调光实验 (saved by Fritzing 0.8.3b)
breadboards: 1

parts:
  R1 = Trimmer Potentiometer [maximum_resistance=10kΩ package=THT]
  元件1 = Arduino Uno (Rev3)
  LED1 = LED - 5mm [color="Red (633nm)" package="5 mm [THT]"]
  R2 = Resistor [tolerance=±5% resistance=1k package=THT]

nets:
  N1: R1.leg1, 元件1.5V, R2.Pin_1
  N2: R1.wiper, 元件1.A0
  N3: R1.leg2, 元件1.GND
  N4: 元件1.D3_PWM, LED1.cathode
  N5: LED1.anode, R2.Pin_0
