# Fritzing sketch 7.无源蜂鸣器实验 (saved by Fritzing 0.8.3b)
breadboards: 1

parts:
  R1 = Trimmer Potentiometer [maximum_resistance=10kΩ package=THT]
  元件1 = Arduino Uno (Rev3)
  J1 = Piezo Speaker

nets:
  N1: R1.leg1, 元件1.5V
  N2: R1.wiper, 元件1.A0
  N3: R1.leg2, 元件1.GND, J1.pin1
  N4: 元件1.D2, J1.pin2
