# Fritzing sketch 8.光敏电阻实验 (saved by Fritzing 0.8.3b)
breadboards: 1

parts:
  元件1 = Arduino Uno (Rev3)
  R1 = Photocell (LDR) [package=THT]
  R2 = Resistor [tolerance=±5% resistance=1k package=THT]

nets:
  N1: 元件1.A5/SCL, R1.pin_0, R2.Pin_1
  N2: 元件1.GND, R1.pin_1
  N3: 元件1.5V, R2.Pin_0
