# Fritzing sketch 9.一位共阴数码管实验 (saved by Fritzing 0.8.3b)

parts:
  元件1 = Arduino Uno (Rev3)
  DI1 = 7-Segment LED Display [package=THT]
  R1 = Resistor [tolerance=±5% resistance=1k package=THT]

nets:
  N1: 元件1.GND, R1.Pin_1
  N2: 元件1.D8, DI1.cathodeG
  N3: 元件1.D9_PWM, DI1.cathodeDP
  N4: 元件1.D2, DI1.cathodeA
  N5: 元件1.D3_PWM, DI1.cathodeB
  N6: 元件1.D4, DI1.cathodeC
  N7: 元件1.D5_PWM, DI1.cathodeD
  N8: 元件1.D6_PWM, DI1.cathodeE
  N9: 元件1.D7, DI1.cathodeF
  N10: DI1.commAnode, R1.Pin_0
